# Fritzing sketch Connections (saved by Fritzing 0.9.3b)

parts:
  Part1 = Arduino Uno (Rev3)
  R1 = Resistor [tolerance=±5% resistance=220 package="0603 [SMD]"]
  S1 = Momentary Switch [package=ksa_sealed_tac_switch]
  HEF1 = HEF4094 [package="DIP16 [THT]"]
  HEF2 = HEF4094 [package="DIP16 [THT]"]
  HEF3 = HEF4094 [package="DIP16 [THT]"]
  HEF4 = HEF4094 [package="DIP16 [THT]"]
  S2 = Momentary Switch [package=ksa_sealed_tac_switch]
  S3 = Momentary Switch [package=ksa_sealed_tac_switch]
  S4 = Momentary Switch [package=ksa_sealed_tac_switch]
  R2 = Resistor [tolerance=±5% resistance=220 package="0603 [SMD]"]
  R3 = Resistor [tolerance=±5% resistance=220 package="0603 [SMD]"]
  R4 = Resistor [tolerance=±5% resistance=220 package="0603 [SMD]"]
  LED1 = LED - 5mm [color="Red (633nm)" package="5 mm [THT]"]
  LED2 = LED - 5mm [color="Red (633nm)" package="5 mm [THT]"]
  R5 = Resistor [tolerance=±5% resistance=220 package="0603 [SMD]"]
  R6 = Resistor [tolerance=±5% resistance=220 package="0603 [SMD]"]
  R7 = Resistor [tolerance=±5% resistance=220 package=THT]
  R8 = Resistor [tolerance=±5% resistance=220 package=THT]
  R9 = Resistor [tolerance=±5% resistance=220 package=THT]
  R10 = Resistor [tolerance=±5% resistance=220 package=THT]
  R11 = Resistor [tolerance=±5% resistance=220 package=THT]
  R12 = Resistor [tolerance=±5% resistance=220 package=THT]
  R13 = Resistor [tolerance=±5% resistance=220 package=THT]
  R14 = Resistor [tolerance=±5% resistance=220 package=THT]
  R15 = Resistor [tolerance=±5% resistance=220 package=THT]
  R16 = Resistor [tolerance=±5% resistance=220 package=THT]
  R17 = Resistor [tolerance=±5% resistance=220 package=THT]
  R18 = Resistor [tolerance=±5% resistance=220 package=THT]
  R19 = Resistor [tolerance=±5% resistance=220 package=THT]
  R20 = Resistor [tolerance=±5% resistance=220 package=THT]
  R21 = Resistor [tolerance=±5% resistance=220 package=THT]
  R22 = Resistor [tolerance=±5% resistance=220 package=THT]
  R23 = Resistor [tolerance=±5% resistance=220 package=THT]
  R24 = Resistor [tolerance=±5% resistance=220 package=THT]
  R26 = Resistor [tolerance=±5% resistance=220 package=THT]
  R27 = Resistor [tolerance=±5% resistance=220 package=THT]
  R28 = Resistor [tolerance=±5% resistance=220 package=THT]
  R29 = Resistor [tolerance=±5% resistance=220 package=THT]
  R30 = Resistor [tolerance=±5% resistance=220 package=THT]
  R31 = Resistor [tolerance=±5% resistance=220 package=THT]
  R32 = Resistor [tolerance=±5% resistance=220 package=THT]
  R33 = Resistor [tolerance=±5% resistance=220 package=THT]
  R34 = Resistor [tolerance=±5% resistance=220 package=THT]
  R35 = Resistor [tolerance=±5% resistance=220 package=THT]
  R36 = Resistor [tolerance=±5% resistance=220 package=THT]
  R37 = Resistor [tolerance=±5% resistance=220 package=THT]
  R38 = Resistor [tolerance=±5% resistance=220 package=THT]
  R39 = Resistor [tolerance=±5% resistance=220 package=THT]
  R40 = Resistor [tolerance=±5% resistance=220 package=THT]
  R41 = Resistor [tolerance=±5% resistance=220 package=THT]

nets:
  N1: Part1.A0, S2.3
  N2: Part1.A1, S3.3
  N3: Part1.A3, S1.3
  N4: Part1.D8, R41.Pin_1
  VSS: Part1.GND, R1.Pin_0, HEF1.Vss, HEF2.Vss, HEF3.Vss, HEF4.Vss, R2.Pin_0, R3.Pin_0, R4.Pin_0, LED1.cathode, LED2.cathode, R10.Pin_0, R15.Pin_0
  N5: Part1.D2, R6.Pin_0
  N6: Part1.D3_PWM, R5.Pin_0
  N7: Part1.D4, HEF1.STROBE, HEF2.STROBE, HEF3.STROBE, HEF4.STROBE
  N8: Part1.D5_PWM, HEF1.DATA
  N9: Part1.D6_PWM, HEF1.CLOCK, HEF2.CLOCK, HEF3.CLOCK, HEF4.CLOCK
  VDD: Part1.5V, S1.2, HEF1.OE, HEF1.Vdd, HEF2.OE, HEF2.Vdd, HEF3.OE, HEF3.Vdd, HEF4.OE, HEF4.Vdd, S2.2, S3.2, S4.2
  N10: R1.Pin_1, S1.4
  N11: HEF1.Q1, R20.Pin_1
  N12: HEF1.Q2, R17.Pin_1
  N13: HEF1.Q3, R18.Pin_1
  N14: HEF1.Q4, R19.Pin_1
  N15: HEF1.Q's, HEF2.DATA
  N16: HEF1.Q8, R9.Pin_0
  N17: HEF1.Q7, R8.Pin_0
  N18: HEF1.Q6, R7.Pin_0
  N19: HEF1.Q5, R11.Pin_0
  N20: HEF2.Q1, R24.Pin_1
  N21: HEF2.Q2, R21.Pin_1
  N22: HEF2.Q3, R22.Pin_1
  N23: HEF2.Q4, R23.Pin_1
  N24: HEF2.Q's, HEF3.DATA
  N25: HEF2.Q8, R14.Pin_0
  N26: HEF2.Q7, R13.Pin_0
  N27: HEF2.Q6, R12.Pin_0
  N28: HEF2.Q5, R16.Pin_0
  N29: HEF3.Q1, R40.Pin_1
  N30: HEF3.Q2, R36.Pin_1
  N31: HEF3.Q3, R38.Pin_1
  N32: HEF3.Q4, R34.Pin_1
  N33: HEF3.Q's, HEF4.DATA
  N34: HEF3.Q8, R29.Pin_0
  N35: HEF3.Q7, R31.Pin_0
  N36: HEF3.Q6, R30.Pin_0
  N37: HEF3.Q5, R32.Pin_0
  N38: HEF4.Q1, R39.Pin_1
  N39: HEF4.Q2, R35.Pin_1
  N40: HEF4.Q3, R37.Pin_1
  N41: HEF4.Q4, R33.Pin_1
  N42: HEF4.Q7, R26.Pin_0
  N43: HEF4.Q6, R27.Pin_0
  N44: HEF4.Q5, R28.Pin_0
  N45: S2.4, R2.Pin_1
  N46: S3.4, R3.Pin_1
  N47: S4.4, R4.Pin_1
  N48: LED1.anode, R5.Pin_1
  N49: LED2.anode, R6.Pin_1

notes:
  7 segment Units
  E F G Dp GND
  A B C D
  7 segment Units
  A B C D
  7 segment Tens
  7 segment Tens
  E F G Dp GND
  14 Segment
  E F G1 G2 L M Dp
  A B C D H I J K
  14 Segment
  1K Ohm
  LEDs
  Override Tropical
  + - Winter Display
  Buttons
  Pump Pin
